# Fritzing sketch LCDI2C (saved by Fritzing 0.9.4)
breadboards: 1

parts:
  Bauteil1 = Adafruit T-Cobbler Plus [part_number="Adafruit #1989 and #2028"]  # not connected
  U1 = LCD-16X2 [package=lcd-16x2_nosilk]
  LCM1602_IIC1 = LCM1602 IIC [part_number="LCM1602 IIC" chip_label="LCM1602 IIC" package="DIP (Dual Inline) [THT]"]

nets:
  VSS: U1.VSS, LCM1602_IIC1.VSS
  VDD: U1.VDD, LCM1602_IIC1.VDD
  N1: U1.VO, LCM1602_IIC1.V0
  N2: U1.RS, LCM1602_IIC1.RS
  N3: U1.R_W, LCM1602_IIC1.RW
  N4: U1.E, LCM1602_IIC1.E
  N5: U1.DB0, LCM1602_IIC1.D0
  N6: U1.DB1, LCM1602_IIC1.D1
  N7: U1.DB2, LCM1602_IIC1.D2
  N8: U1.DB3, LCM1602_IIC1.D3
  N9: U1.DB4, LCM1602_IIC1.D4
  N10: U1.DB5, LCM1602_IIC1.D5
  N11: U1.DB6, LCM1602_IIC1.D6
  N12: U1.DB7, LCM1602_IIC1.D7
  N13: U1.A, LCM1602_IIC1.A
  N14: U1.K, LCM1602_IIC1.K

custom parts:
  Adafruit T-Cobbler Plus: The Raspberry Pi has landed on the Maker World like a 40-GPIO pinned, quad-USB ported, credit card sized bomb of DIY joy. And while you can use most of our great Model B accessories by hooking up our downgrade cable, its probably a good time to upgrade your set up and accessorize using all of the 40 pins. That's why we now carry the Assembled Adafruit Pi T-Cobbler Plus - Breakout + Cable for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
  LCM1602 IIC: I2C-Module to use a 1602 or 2004 LCD on with the wire.h libory Serial LCD Modul
