# Fritzing sketch grove_rfid_reader (saved by Fritzing 0.9.4)
breadboards: 1

parts:
  Bauteil1 = Adafruit T-Cobbler Plus [part_number="Adafruit #1989 and #2028"]  # not connected
  JP1 = Header 4 [package=screwterminal-3.5mm-4_lock]
  U2 = MLX90121 [package=ssop20]

nets:
  N1: JP1.1, U2.XOUT
  N2: JP1.2, U2.VSS1
  N3: JP1.3, U2.MOD
  N4: JP1.4, U2.TX

notes:
  Grove RFID Reader
  Grove Cable
  Grove Adaptor

custom parts:
  Adafruit T-Cobbler Plus: The Raspberry Pi has landed on the Maker World like a 40-GPIO pinned, quad-USB ported, credit card sized bomb of DIY joy. And while you can use most of our great Model B accessories by hooking up our downgrade cable, its probably a good time to upgrade your set up and accessorize using all of the 40 pins. That's why we now carry the Assembled Adafruit Pi T-Cobbler Plus - Breakout + Cable for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
