# Fritzing sketch grove_serial_cam (saved by Fritzing 0.9.4)
breadboards: 1

parts:
  Bauteil1 = Adafruit T-Cobbler Plus [part_number="Adafruit #1989 and #2028"]  # not connected
  U1 = TRANSCHIPTC5747 [package=camera_sfv24r-2st_2]
  JP1 = Header 4 [package=screwterminal-3.5mm-4_lock]

nets:
  N1: U1.CLK_IN, JP1.4
  N2: U1.DGND, JP1.1
  N3: U1.DOUT_0, JP1.2
  N4: U1.DOUT_1, JP1.3

notes:
  Grove Serial Camera
  Grove Cable (Glued to Camera)
  Grove Adaptor

custom parts:
  Adafruit T-Cobbler Plus: The Raspberry Pi has landed on the Maker World like a 40-GPIO pinned, quad-USB ported, credit card sized bomb of DIY joy. And while you can use most of our great Model B accessories by hooking up our downgrade cable, its probably a good time to upgrade your set up and accessorize using all of the 40 pins. That's why we now carry the Assembled Adafruit Pi T-Cobbler Plus - Breakout + Cable for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
