# Fritzing sketch motor (saved by Fritzing 0.9.4)
breadboards: 1

parts:
  Bauteil1 = Adafruit T-Cobbler Plus [part_number="Adafruit #1989 and #2028"]  # not connected
  IC1 = L293D [package=THT]
  M1 = DC Motor

nets:
  N1: IC1.Enable_1, IC1.+Vmotor, IC1.+V
  N2: IC1.Out_1_(_Controlled_by_Enable_1_), M1.pin_1
  N3: IC1.Out_2_(_Controlled_by_Enable_1_), M1.pin_2

custom parts:
  Adafruit T-Cobbler Plus: The Raspberry Pi has landed on the Maker World like a 40-GPIO pinned, quad-USB ported, credit card sized bomb of DIY joy. And while you can use most of our great Model B accessories by hooking up our downgrade cable, its probably a good time to upgrade your set up and accessorize using all of the 40 pins. That's why we now carry the Assembled Adafruit Pi T-Cobbler Plus - Breakout + Cable for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
